# Fritzing sketch Untitled Sketch 2 (saved by Fritzing 0.9.3b)
breadboards: 1

parts:
  MH-ET_LIVE_ESP32_DEVKIT2 = MH-ET LIVE ESP32 DEVKIT 38 pins
  Keyes1 = Keyes IR Infrared Sensor Switch Module
  Keyes2 = Keyes IR Infrared Sensor Switch Module
  Keyes3 = Keyes IR Infrared Sensor Switch Module
  Keyes4 = Keyes IR Infrared Sensor Switch Module
  LCD2 = LCD screen
  LCM1602_IIC3 = LCM1602 IIC [part_number="LCM1602 IIC" chip_label="LCM1602 IIC" package="DIP (Dual Inline) [THT]"]

nets:
  VCC: MH-ET_LIVE_ESP32_DEVKIT2.3V3, Keyes1.VCC, Keyes2.VCC, Keyes3.VCC, Keyes4.VCC
  N1: MH-ET_LIVE_ESP32_DEVKIT2.IO14, Keyes4.out
  N2: MH-ET_LIVE_ESP32_DEVKIT2.IO12, Keyes1.out
  GND: MH-ET_LIVE_ESP32_DEVKIT2.GND#58, Keyes1.GND, Keyes2.GND, Keyes3.GND, Keyes4.GND
  5V: MH-ET_LIVE_ESP32_DEVKIT2.5V, LCM1602_IIC3.VCC
  N3: MH-ET_LIVE_ESP32_DEVKIT2.GND#64, LCM1602_IIC3.GND
  N4: MH-ET_LIVE_ESP32_DEVKIT2.IO22, LCM1602_IIC3.SCL
  N5: MH-ET_LIVE_ESP32_DEVKIT2.IO21, LCM1602_IIC3.SDA
  N6: MH-ET_LIVE_ESP32_DEVKIT2.IO2, Keyes3.out
  N7: MH-ET_LIVE_ESP32_DEVKIT2.IO15, Keyes2.out
  VSS: LCD2.VSS, LCM1602_IIC3.VSS
  VDD: LCD2.VDD, LCM1602_IIC3.VDD
  N8: LCD2.V0, LCM1602_IIC3.V0
  N9: LCD2.RS, LCM1602_IIC3.RS
  N10: LCD2.R/W, LCM1602_IIC3.RW
  N11: LCD2.E, LCM1602_IIC3.E
  N12: LCD2.DB0, LCM1602_IIC3.D0
  N13: LCD2.DB1, LCM1602_IIC3.D1
  N14: LCD2.DB2, LCM1602_IIC3.D2
  N15: LCD2.DB3, LCM1602_IIC3.D3
  N16: LCD2.DB4, LCM1602_IIC3.D4
  N17: LCD2.DB5, LCM1602_IIC3.D5
  N18: LCD2.DB6, LCM1602_IIC3.D6
  N19: LCD2.DB7, LCM1602_IIC3.D7
  N20: LCD2.LED+, LCM1602_IIC3.A
  N21: LCD2.LED-, LCM1602_IIC3.K
  N22: LCM1602_IIC3.LED_A, LCM1602_IIC3.LED_B

notes:
  IR Sensor 01
  IR Sensor 02
  IR Sensor 03
  IR Sensor 04
  Esp32 Microcontroller

custom parts:
  MH-ET LIVE ESP32 DEVKIT 38 pins: http://mh.nodebb.com/topic/2/mh-et-live-esp32-devkit
  Keyes IR Infrared Sensor Switch Module: An infrared obstacle detector
  LCM1602 IIC: I2C-Module to use a 1602 or 2004 LCD on with the wire.h libory Serial LCD Modul
